# Fritzing sketch AmpPCB (saved by Fritzing 0.9.3b)
circuit board: 1.8cm x 2.1cm
circuit board: 7.14963cm x 3.62749cm
circuit board: 1.8cm x 2.1cm
circuit board: 1.8cm x 2.1cm
breadboards: 1

parts:
  J15 = male pin header, 2 pins [form="♂ (male)"]
  J16 = male pin header, 2 pins [form="♂ (male)"]
  J17 = male pin header, 3 pins [form="♂ (male)"]
  J18 = male pin header, 2 pins [form="♂ (male)"]
  J19 = screw terminal, 2 pins
  J20 = male pin header, 2 pins [form="♂ (male)"]
  J21 = male pin header, 2 pins [form="♂ (male)"]
  J22 = male pin header, 3 pins [form="♂ (male)"]
  J23 = male pin header, 2 pins [form="♂ (male)"]
  J24 = male pin header, 2 pins [form="♂ (male)"]
  J25 = male pin header, 3 pins [form="♂ (male)"]
  J26 = male pin header, 2 pins [form="♂ (male)"]
  J27 = male pin header, 2 pins [form="♂ (male)"]
  J28 = screw terminal, 2 pins
  J29 = screw terminal, 2 pins
  J30 = screw terminal, 2 pins
  J31 = screw terminal, 2 pins
  J32 = screw terminal, 2 pins
  J33 = screw terminal, 2 pins
  J34 = screw terminal, 3 pins
  J35 = screw terminal, 3 pins
  J36 = screw terminal, 3 pins

nets:
  N1: J15.pin1, J29.pin2
  N2: J15.pin2, J29.pin1
  N3: J16.pin1, J28.pin2
  N4: J16.pin2, J28.pin1
  N5: J17.pin1, J36.pin1
  N6: J17.pin2, J36.pin2
  N7: J17.pin3, J36.pin3
  N8: J18.pin1, J19.pin2, J20.pin1, J27.pin1
  N9: J18.pin2, J19.pin1, J20.pin2, J27.pin2
  N10: J21.pin1, J30.pin2
  N11: J21.pin2, J30.pin1
  N12: J22.pin1, J35.pin1
  N13: J22.pin2, J35.pin2
  N14: J22.pin3, J35.pin3
  N15: J23.pin1, J31.pin2
  N16: J23.pin2, J31.pin1
  N17: J24.pin1, J32.pin2
  N18: J24.pin2, J32.pin1
  N19: J25.pin1, J34.pin1
  N20: J25.pin2, J34.pin2
  N21: J25.pin3, J34.pin3
  N22: J26.pin1, J33.pin2
  N23: J26.pin2, J33.pin1
